# Fritzing sketch DHT-11 circuit (saved by Fritzing 0.9.0b)
breadboards: 1

parts:
  Raspberry_Pi1 = Raspberry Pi (Model B)
  DHT1 = DHT11 Humitidy and Temperature Sensor
  C2 = Tantalum Capacitor [capacitance=1μF package="100 mil [THT, tantalum]"]
  R1 = Resistor [tolerance=±5% resistance=220 package=THT]
  C3 = Tantalum Capacitor [capacitance=1μF package="100 mil [THT, tantalum]"]

nets:
  3V3: Raspberry_Pi1.3V3, DHT1.VDD, R1.Pin_0
  GND: Raspberry_Pi1.GND, Raspberry_Pi1.#4, DHT1.DATA, DHT1.GND, C2.+, R1.Pin_1, C3.+
  N1: Raspberry_Pi1.#17, C3.-
  N2: Raspberry_Pi1.MISO, C2.-

custom parts:
  Raspberry Pi (Model B): Raspberry Pi Single-board Computer, Model B
  DHT11 Humitidy and Temperature Sensor: DHT11 Humidity and Temperature Sensor
